// Logisim project DM-02.circ as structural Verilog: 12 circuits, main circuit DM-02
module DM_02 (
  input  [7:0] in_1,
  input  in_2,
  input  in_3,
  input  in_4,
  input  in_5,
  output [4:0] FLAGS__DNZOC,
  output [4:0] out_7,
  output Carry,
  output Overflow,
  output Zero,
  output Negative,
  output [3:0] out_12,
  output [3:0] out_13,
  output [7:0] out_14,
  output [15:0] CONTROLWORD
);

  wire A_clock, A_load, ALU_clock, ALU_load, and_1_out, and_2_out, and_3_out, and_4_out, and_5_out,
       and_6_out, and_7_out, and_8_out, and_9_out, and_10_out, and_13_out, and_20_out, B_clock, B_load,
       button_1_out, C_clock, C_load, CLOCK1, CLOCK2, clock_1_out, CLOCK_halt, clock_phases_1_halted,
       CONTINUE_out, d_ff_1_q, d_ff_2_q, F_clock, F_load, FETCH_0, FETCH_1, FETCH_DONE, H_clock, H_load,
       ic_74138_1_p4, ic_74138_1_p5, ic_74138_1_p6, ic_74138_2_p7, ic_74138_2_p8, ic_74138_2_p9,
       ic_74138_2_p11, ic_74138_2_p12, ic_74163_1_p6, ic_74163_1_p7, ic_74163_1_p8, ic_74244_1_p3,
       ic_74244_1_p4, ic_74244_1_p5, ic_74244_1_p6, ic_74244_2_p16, IO_EN, IR_load, L_clock, L_load, MAR_inc,
       MEM_out, n74154_1_p1, n74154_1_p2, n74154_1_p3, n74154_1_p4, n74154_1_p5, n74154_1_p6, n74154_1_p7,
       n74154_1_p8, n74154_1_p9, n74154_1_p10, n74154_1_p15, n74154_1_p17, n74154_1_p18, n74154_1_p19,
       n74154_1_p20, n74154_2_p4, n74154_2_p5, n74154_2_p6, n74154_2_p7, n74154_2_p8, n74154_2_p9,
       n74154_2_p10, n74154_2_p11, n74154_2_p12, n74154_2_p13, n74154_2_p14, n74154_2_p15, n74154_2_p16,
       n74154_2_p17, n74154_2_p22, n74154_2_p27, n74154_2_p28, n74154_3_p7, n74154_3_p13, n74154_4_p1,
       n74154_4_p2, n74154_4_p3, n74154_4_p4, n74154_4_p5, n74154_4_p6, n74154_4_p7, n74154_4_p11,
       n74154_4_p16, n74154_4_p18, n74154_4_p19, n74154_4_p20, n74161_bus_3_tc, n74161_bus_4_tc,
       n74161_bus_5_tc, n74191_bus_2_nrco, n74191_bus_3_nrco, n74191_bus_4_nrco, nA_out, nand_1_out,
       nand_2_out, nand_3_out, nand_4_out, nand_5_out, nand_6_out, nB_out, nC_out, nCLOCK1, nCLOCK2, nCMP,
       nF_out, nFCLR_c, nFCLR_z, nFSET_c, nFSET_z, nH_out, nL_out, nMAR_H_load, nMAR_H_reg_load, nMAR_L_load,
       nMAR_L_reg_load, nMEM_load, nMEM_out, nor_1_out, nor_2_out, nor_3_out, nor_5_out, nor_7_out,
       nor_10_out, not_1_out, not_2_out, not_4_out, not_5_out, not_9_out, not_10_out, not_11_out, not_12_out,
       not_13_out, not_16_out, not_17_out, nPC_H_out, nPC_L_out, nPC_MAR_transfer, nRESET, nROM_EN,
       nSTK_CLK_EN, nSTK_H_out, nSTK_L_out, nSTK_MAR_transfer, or_1_out, or_2_out, or_3_out, or_4_out,
       or_5_out, or_6_out, or_8_out, or_9_out, or_10_out, PC_H_load, PC_inc_rom, PC_L_load, PC_MAR_transfer,
       RAM_EN, STK_dec, STK_DOWN_nUP, STK_H_load, STK_inc, STK_L_load, TSTATE_MAX, TSTATE_reset;
  wire [3:0] A_q, A_q_2, B_p, B_p_2, C_p, C_p_2, H_p, H_p_2, IR_p, IR_p_2, L_p, n74161_bus_2_q,
       n74161_bus_3_q, n74161_bus_4_q, n74161_bus_5_q, n74161_bus_6_q, n74191_bus_1_q, n74191_bus_2_q,
       n74377_bus_2_q, n74377_bus_2_q_2, rom_2_data, rom_2_data_2;
  wire [7:0] cscvon8_alu_1_p2, cscvon8_alu_1_p4, IO_ADDRESS, n74191_bus_4_q, n74245_bus_1_b;
  wire [7:4] L_p_2;
  wire [15:0] ADDRESS;

  LED led_1 (.in(clock_phases_1_halted));
  Button button_1 (.out(button_1_out));
  Button CONTINUE (.out(CONTINUE_out));
  and and_1 (and_1_out, ALU_clock, nCMP);
  Pull_Resistor pull_resistor_1 (.node(in_1[0]));
  Pull_Resistor pull_resistor_2 (.node(in_1[1]));
  Pull_Resistor pull_resistor_3 (.node(in_1[2]));
  Pull_Resistor pull_resistor_4 (.node(in_1[3]));
  Pull_Resistor pull_resistor_5 (.node(in_1[4]));
  Pull_Resistor pull_resistor_6 (.node(in_1[5]));
  Pull_Resistor pull_resistor_7 (.node(in_1[6]));
  Pull_Resistor pull_resistor_8 (.node(in_1[7]));
  not not_1 (not_1_out, ALU_load);
  not not_2 (not_2_out, F_load);
  not not_3 (nRESET, in_3);
  and and_2 (and_2_out, CLOCK1, FETCH_0);
  Clock clock_1 (.out(clock_1_out));
  or or_1 (or_1_out, button_1_out, CLOCK_halt);
  nor nor_1 (nor_1_out, A_clock, and_1_out);
  nor nor_2 (nor_2_out, ALU_load, ALU_load);
  nor nor_3 (nor_3_out, A_load, A_load);
  or or_2 (or_2_out, ALU_clock, F_clock);
  // IC_74244 ic_74244_1: pin names not known; wires that end beside it: not_1_out, not_2_out, ic_74244_1_p3, ic_74244_1_p4, ic_74244_1_p5, ic_74244_1_p6, ic_74244_1_p3, ic_74244_1_p4, ic_74244_1_p5, ic_74244_1_p6
  nor nor_4 (STK_DOWN_nUP, STK_inc, nor_5_out);
  nor nor_5 (nor_5_out, STK_DOWN_nUP, STK_dec);
  nor nor_6 (nSTK_CLK_EN, STK_dec, STK_inc);
  or or_3 (or_3_out, nCLOCK1, and_2_out);
  not not_4 (not_4_out, FETCH_DONE);
  or or_4 (or_4_out, not_4_out, or_5_out);
  not not_5 (not_5_out, nRESET);
  and and_3 (and_3_out, FETCH_0, nCLOCK2);
  Clock_Phases clock_phases_1 (
    .CLOCK(clock_1_out), .HALT(or_1_out), .CONTINUE(CONTINUE_out), .HALTED(clock_phases_1_halted),
    .CLOCK1(CLOCK1), .CLOCK2(CLOCK2), .nCLOCK1(nCLOCK1), .nCLOCK2(nCLOCK2));
  nor nor_7 (nor_7_out, nor_1_out, nor_1_out);
  _74245_Bus u_74245_bus_1 (.A(cscvon8_alu_1_p4), .nOE(nor_2_out), .B(n74245_bus_1_b));
  _74245_Bus u_74245_bus_2 (.A(in_1), .nOE(nor_3_out), .B(n74245_bus_1_b));
  and and_4 (and_4_out, ALU_clock, nCMP);
  nand nand_1 (nand_1_out, STK_H_load, CLOCK2);
  nand nand_2 (nand_2_out, CLOCK2, STK_L_load);
  and and_5 (and_5_out, or_3_out, or_4_out);
  or or_5 (or_5_out, not_5_out, TSTATE_reset, TSTATE_MAX);
  nor nor_8 (nPC_MAR_transfer, and_3_out, PC_MAR_transfer);
  and and_6 (and_6_out, FETCH_1, CLOCK2);
  and and_7 (and_7_out, PC_inc_rom, CLOCK1);
  Hex_Digit_Display hex_digit_display_1 (.value(A_q));  // open: dp
  Hex_Digit_Display hex_digit_display_2 (.value(A_q_2));  // open: dp
  _74377_Bus A (.D(n74245_bus_1_b), .CLK(nor_7_out), .nCE(1'b0), .Q({A_q_2, A_q}));
  or or_6 (or_6_out, A_clock, and_4_out);
  Hex_Digit_Display hex_digit_display_3 (.value(n74191_bus_1_q));  // open: dp
  // IC_74163 ic_74163_1: pin names not known; wires that end beside it: and_5_out, 1'b1, 1'b1, or_5_out, 1'b1, ic_74163_1_p6, ic_74163_1_p7, ic_74163_1_p8, ic_74163_1_p6, ic_74163_1_p7, ic_74163_1_p8
  nor nor_9 (nMEM_out, FETCH_0, MEM_out);
  or or_7 (IR_load, and_6_out, and_7_out);
  D_Flip_Flop d_ff_1 (.clk(and_7_out), .D(and_7_out), .Q(d_ff_1_q), .en(1'b1), .reset(in_5));  // open: Qn, preset
  Hex_Digit_Display hex_digit_display_4 (.value(in_1[3:0]));  // open: dp
  Hex_Digit_Display hex_digit_display_5 (.value(in_1[7:4]));  // open: dp
  _74245_Bus u_74245_bus_3 (.A({A_q_2, A_q}), .nOE(nA_out), .B(in_1));
  // IC_74377 ic_74377_1: pin names not known; wires that end beside it: or_6_out
  // DIP_7474 dip_7474_1: pin names not known; wires that end beside it: 1'b0, nFCLR_c, ic_74244_1_p3, or_2_out, nFSET_c, Carry, nFCLR_z, nFSET_z, ic_74244_1_p5, or_2_out, out_13[2]
  Hex_Digit_Display hex_digit_display_6 (.value(n74191_bus_2_q));  // open: dp
  Hex_Digit_Display hex_digit_display_7 (.value(n74191_bus_4_q[7:4]));  // open: dp
  _74191_Bus u_74191_bus_1 (
    .nU_D(STK_DOWN_nUP), .CK(n74191_bus_2_nrco), .nCTEN(nSTK_CLK_EN), .nPL(nand_1_out), .Q(n74191_bus_1_q),
    .D(in_1[7:4]));  // open: TC, nRCO
  // IC_74138 ic_74138_1: pin names not known; wires that end beside it: 1'b0, 1'b0, nRESET, ic_74138_1_p4, ic_74138_1_p5, ic_74138_1_p6
  Hex_Digit_Display hex_digit_display_8 (.value(B_p));  // open: dp
  Hex_Digit_Display hex_digit_display_9 (.value(B_p_2));  // open: dp
  _74574_Peek B (.nOE(nB_out), .CLK(B_clock), .D(in_1), .Q(in_1), .P({B_p_2, B_p}));
  // CSCvon8_ALU cscvon8_alu_1: pin names not known; wires that end beside it: in_1, cscvon8_alu_1_p2, CONTROLWORD[5:1], cscvon8_alu_1_p4, FLAGS__DNZOC, 1'b1
  Hex_Digit_Display hex_digit_display_10 (.value(n74191_bus_4_q[3:0]));  // open: dp
  _74191_Bus u_74191_bus_2 (
    .nU_D(STK_DOWN_nUP), .CK(n74191_bus_3_nrco), .nCTEN(nSTK_CLK_EN), .nPL(nand_1_out),
    .nRCO(n74191_bus_2_nrco), .Q(n74191_bus_2_q), .D(in_1[3:0]));  // open: TC
  not not_6 (FETCH_0, ic_74138_1_p4);
  not not_7 (FETCH_1, ic_74138_1_p5);
  not not_8 (FETCH_DONE, ic_74138_1_p6);
  D_Flip_Flop d_ff_2 (.clk(IR_load), .D(IR_load), .Q(d_ff_2_q), .en(1'b1), .reset(in_4));  // open: Qn, preset
  Hex_Digit_Display hex_digit_display_11 (.value(cscvon8_alu_1_p4[3:0]));  // open: dp
  Hex_Digit_Display hex_digit_display_12 (.value(cscvon8_alu_1_p4[7:4]));  // open: dp
  // DIP_7474 dip_7474_2: pin names not known; wires that end beside it: 1'b1, ic_74244_1_p4, or_2_out, 1'b1, out_13[1], 1'b1, 1'b1, ic_74244_1_p6, or_2_out, Negative
  Hex_Digit_Display hex_digit_display_13 (.value(C_p));  // open: dp
  Hex_Digit_Display hex_digit_display_14 (.value(C_p_2));  // open: dp
  _74574_Peek C (.nOE(nC_out), .CLK(C_clock), .D(in_1), .Q(in_1), .P({C_p_2, C_p}));
  _74245_Bus u_74245_bus_4 (.A(n74191_bus_4_q), .nOE(nSTK_L_out), .B(in_1));
  _74245_Bus u_74245_bus_5 (.A({n74191_bus_1_q, n74191_bus_2_q}), .nOE(nSTK_H_out), .B(in_1));
  _74245_Bus u_74245_bus_6 (.A(n74191_bus_4_q), .nOE(nSTK_MAR_transfer), .B(ADDRESS[7:0]));
  _74245_Bus u_74245_bus_7 (.A({n74191_bus_1_q, n74191_bus_2_q}), .nOE(nSTK_MAR_transfer), .B(ADDRESS[15:8]));
  _74191_Bus u_74191_bus_3 (
    .nU_D(STK_DOWN_nUP), .CK(n74191_bus_4_nrco), .nCTEN(nSTK_CLK_EN), .nPL(nand_2_out),
    .nRCO(n74191_bus_3_nrco), .Q(n74191_bus_4_q[7:4]), .D(in_1[7:4]));  // open: TC
  not not_9 (not_9_out, TSTATE_reset);
  and and_8 (and_8_out, not_9_out, FETCH_DONE);
  Pull_Resistor pull_resistor_9 (.node(out_13[1]));
  Pull_Resistor pull_resistor_10 (.node(Negative));
  Pull_Resistor pull_resistor_11 (.node(out_13[2]));
  Pull_Resistor pull_resistor_12 (.node(Carry));
  _74191_Bus u_74191_bus_4 (
    .nU_D(STK_DOWN_nUP), .CK(CLOCK2), .nCTEN(nSTK_CLK_EN), .nPL(nand_2_out), .nRCO(n74191_bus_4_nrco),
    .Q(n74191_bus_4_q[3:0]), .D(in_1[3:0]));  // open: TC
  _74161_Bus u_74161_bus_1 (
    .CLK(nCLOCK1), .nCLR(and_8_out), .nPE(1'b1), .CEP(1'b1), .CET(1'b1), .Q(out_12), .TC(TSTATE_MAX));  // open: D
  Hex_Digit_Display hex_digit_display_15 (.value(H_p));  // open: dp
  Hex_Digit_Display hex_digit_display_16 (.value(H_p_2));  // open: dp
  _74574_Peek H (.nOE(nH_out), .CLK(H_clock), .D(in_1), .Q(in_1), .P({H_p_2, H_p}));
  or or_8 (or_8_out, IR_load, PC_H_load);
  Hex_Digit_Display hex_digit_display_17 (.value(n74161_bus_2_q));  // open: dp
  Pull_Resistor pull_resistor_13 (.node(TSTATE_MAX));
  and and_9 (and_9_out, or_8_out, CLOCK2);
  nand nand_3 (nand_3_out, PC_H_load, CLOCK1);
  Hex_Digit_Display hex_digit_display_18 (.value(n74161_bus_3_q));  // open: dp
  Hex_Digit_Display hex_digit_display_19 (.value(n74161_bus_4_q));  // open: dp
  Pull_Resistor pull_resistor_14 (.node(out_12[0]));
  Pull_Resistor pull_resistor_15 (.node(out_12[1]));
  Pull_Resistor pull_resistor_16 (.node(out_12[2]));
  Pull_Resistor pull_resistor_17 (.node(out_12[3]));
  Hex_Digit_Display hex_digit_display_20 (.value(L_p));  // open: dp
  Hex_Digit_Display hex_digit_display_21 (.value(L_p_2));  // open: dp
  _74574_Peek L (.nOE(nL_out), .CLK(L_clock), .D(in_1), .Q(in_1), .P({L_p_2, L_p}));
  _74161_Bus u_74161_bus_2 (
    .CLK(and_9_out), .nCLR(nRESET), .nPE(nand_3_out), .CEP(n74161_bus_3_tc), .CET(n74161_bus_3_tc),
    .D(in_1[7:4]), .Q(n74161_bus_2_q));  // open: TC
  Hex_Digit_Display hex_digit_display_22 (.value(n74161_bus_5_q));  // open: dp
  Hex_Digit_Display hex_digit_display_23 (.value(out_14[7:4]));  // open: dp
  _74245_Bus u_74245_bus_8 (.A(in_1), .nOE(nMAR_L_load), .B(ADDRESS[7:0]));
  _74245_Bus u_74245_bus_9 (.A(in_1), .nOE(nMAR_H_load), .B(ADDRESS[15:8]));
  and and_10 (and_10_out, nPC_MAR_transfer, nSTK_MAR_transfer);
  Hex_Digit_Display hex_digit_display_24 (.value(out_12));  // open: dp
  Hex_Digit_Display hex_digit_display_25 (.value(out_14[3:0]));  // open: dp
  Hex_Digit_Display hex_digit_display_26 (.value(IR_p));  // open: dp
  Hex_Digit_Display hex_digit_display_27 (.value(IR_p_2));  // open: dp
  _74574_Peek IR (.nOE(1'b0), .CLK(IR_load), .D(in_1), .Q(out_14), .P({IR_p_2, IR_p}));
  _74161_Bus u_74161_bus_3 (
    .CLK(and_9_out), .nCLR(nRESET), .nPE(nand_3_out), .CEP(n74161_bus_4_tc), .CET(n74161_bus_4_tc),
    .D(in_1[3:0]), .Q(n74161_bus_3_q), .TC(n74161_bus_3_tc));
  and and_11 (nMAR_H_reg_load, nMAR_H_load, and_10_out);
  and and_12 (nMAR_L_reg_load, and_10_out, nMAR_L_load);
  Hex_Digit_Display hex_digit_display_28 (.value({Negative, out_13[2:1], Carry}));  // open: dp
  ROM #(.addrWidth(16), .dataWidth(16)) rom_1 (
    .addr({out_14, out_12, Negative, out_13[2:1], Carry}), .data(CONTROLWORD), .sel(FETCH_DONE));
  Pull_Resistor pull_resistor_18 (.node(CONTROLWORD));
  Pull_Resistor pull_resistor_19 (.node(out_14[7]));
  Pull_Resistor pull_resistor_20 (.node(out_14[5]));
  Pull_Resistor pull_resistor_21 (.node(out_14[4]));
  Pull_Resistor pull_resistor_22 (.node(out_14[6]));
  Pull_Resistor pull_resistor_23 (.node(out_14[3]));
  _74245_Bus u_74245_bus_10 (.A({n74161_bus_4_q, n74161_bus_5_q}), .nOE(nPC_L_out), .B(in_1));
  _74245_Bus u_74245_bus_11 (.A({n74161_bus_2_q, n74161_bus_3_q}), .nOE(nPC_H_out), .B(in_1));
  _74245_Bus u_74245_bus_12 (.A({n74161_bus_4_q, n74161_bus_5_q}), .nOE(nPC_MAR_transfer), .B(ADDRESS[7:0]));
  _74245_Bus u_74245_bus_13 (.A({n74161_bus_2_q, n74161_bus_3_q}), .nOE(nPC_MAR_transfer), .B(ADDRESS[15:8]));
  Pull_Resistor pull_resistor_24 (.node(out_14[0]));
  Pull_Resistor pull_resistor_25 (.node(out_14[2]));
  Pull_Resistor pull_resistor_26 (.node(out_14[1]));
  _74161_Bus u_74161_bus_4 (
    .CLK(and_13_out), .nCLR(nRESET), .nPE(nand_4_out), .CEP(n74161_bus_5_tc), .CET(n74161_bus_5_tc),
    .D(in_1[7:4]), .Q(n74161_bus_4_q), .TC(n74161_bus_4_tc));
  Hex_Digit_Display hex_digit_display_29 (.value(n74377_bus_2_q));  // open: dp
  Hex_Digit_Display hex_digit_display_30 (.value(n74377_bus_2_q_2));  // open: dp
  Hex_Digit_Display hex_digit_display_31 (.value(IO_ADDRESS[3:0]));  // open: dp
  Hex_Digit_Display hex_digit_display_32 (.value(IO_ADDRESS[7:4]));  // open: dp
  _74377_Bus u_74377_bus_1 (.D(ADDRESS[7:0]), .CLK(nCLOCK2), .nCE(nMAR_L_reg_load), .Q(IO_ADDRESS));
  _74377_Bus u_74377_bus_2 (
    .D(ADDRESS[15:8]), .CLK(nCLOCK2), .nCE(nMAR_H_reg_load), .Q({n74377_bus_2_q_2, n74377_bus_2_q}));
  not not_10 (not_10_out, nCLOCK2);
  _74161_Bus u_74161_bus_5 (
    .CLK(and_13_out), .nCLR(nRESET), .nPE(nand_4_out), .CEP(1'b1), .CET(1'b1), .D(in_1[3:0]),
    .Q(n74161_bus_5_q), .TC(n74161_bus_5_tc));
  // IC_74244 ic_74244_2: pin names not known; wires that end beside it: A_load, B_load, C_load, H_load, L_load, IR_load, ALU_load, F_load, not_10_out, not_10_out, A_clock, B_clock, C_clock, H_clock, L_clock, ic_74244_2_p16, ALU_clock, F_clock
  and and_13 (and_13_out, or_9_out, CLOCK2);
  nand nand_4 (nand_4_out, PC_L_load, CLOCK1);
  Pull_Resistor pull_resistor_27 (.node(C_clock));
  Pull_Resistor pull_resistor_28 (.node(F_clock));
  Pull_Resistor pull_resistor_29 (.node(ALU_clock));
  Pull_Resistor pull_resistor_30 (.node(ic_74244_2_p16));
  Pull_Resistor pull_resistor_31 (.node(L_clock));
  Pull_Resistor pull_resistor_32 (.node(A_clock));
  Pull_Resistor pull_resistor_33 (.node(B_clock));
  Pull_Resistor pull_resistor_34 (.node(H_clock));
  or or_9 (or_9_out, IR_load, PC_L_load);
  not not_11 (not_11_out, nROM_EN);
  or or_10 (or_10_out, n74377_bus_2_q_2[2], n74377_bus_2_q_2[3]);
  Hex_Digit_Display hex_digit_display_33 (.value(rom_2_data_2));  // open: dp
  ROM #(.addrWidth(16)) rom_2 (
    .addr({n74377_bus_2_q_2, n74377_bus_2_q, IO_ADDRESS}), .data({rom_2_data_2, rom_2_data}), .sel(not_11_out));
  RAM #(.addrWidth(16)) ram_1 (
    .addr({n74377_bus_2_q_2, n74377_bus_2_q, IO_ADDRESS}), .data({rom_2_data_2, rom_2_data}), .sel(RAM_EN));  // open: clk, ld, clr
  and and_14 (IO_EN, n74377_bus_2_q[0], n74377_bus_2_q[1], n74377_bus_2_q[2], n74377_bus_2_q[3], n74377_bus_2_q_2[0], n74377_bus_2_q_2[1], n74377_bus_2_q_2[2], n74377_bus_2_q_2[3]);
  nand nand_5 (nand_5_out, or_10_out, nand_6_out);
  nand nand_6 (nand_6_out, IO_EN, IO_EN);
  or or_11 (nROM_EN, IO_EN, RAM_EN);
  Hex_Digit_Display hex_digit_display_34 (.value(rom_2_data));  // open: dp
  nand nand_7 (RAM_EN, nand_5_out, nand_5_out);
  _74245_Bus u_74245_bus_14 (.A({rom_2_data_2, rom_2_data}), .nOE(nMEM_out), .B(in_1));
  _74245_Bus u_74245_bus_15 (.A(in_1), .nOE(nMEM_load), .B({rom_2_data_2, rom_2_data}));
  nand nand_8 (TSTATE_reset, n74154_1_p1, n74154_2_p7);
  nand nand_9 (CLOCK_halt, n74154_1_p2, n74154_2_p8);
  nand nand_10 (STK_inc, n74154_1_p3, n74154_2_p9);
  nand nand_11 (STK_dec, n74154_1_p4, n74154_2_p10);
  nand nand_12 (PC_inc_rom, n74154_1_p5, n74154_2_p11);
  nand nand_13 (PC_MAR_transfer, n74154_1_p6, n74154_2_p12);
  and and_15 (nSTK_MAR_transfer, n74154_1_p7, n74154_2_p13);
  nand nand_14 (MAR_inc, n74154_1_p8, n74154_2_p14);
  and and_16 (nFSET_z, n74154_1_p9, n74154_2_p15);
  and and_17 (nFSET_c, n74154_1_p10, n74154_2_p16);
  and and_18 (nFCLR_z, n74154_2_p17, n74154_2_p28);
  and and_19 (nFCLR_c, n74154_1_p20, n74154_2_p27);
  not not_12 (not_12_out, nRESET);
  not not_13 (not_13_out, FETCH_DONE);
  not not_14 (nCMP, in_2);
  nor nor_10 (nor_10_out, not_12_out, TSTATE_reset, TSTATE_MAX);
  and and_20 (and_20_out, nCLOCK1, not_13_out);
  // _74154 74154_1: pin names not known; wires that end beside it: n74154_1_p1, n74154_1_p2, n74154_1_p3, n74154_1_p4, n74154_1_p5, n74154_1_p6, n74154_1_p7, n74154_1_p8, n74154_1_p9, n74154_1_p10, CONTROLWORD[1], CONTROLWORD[2], CONTROLWORD[3], CONTROLWORD[4], n74154_1_p15, n74154_1_p15, n74154_1_p17, n74154_1_p18, n74154_1_p19, n74154_1_p20
  // _74154 74154_2: pin names not known; wires that end beside it: n74154_1_p19, n74154_1_p18, n74154_1_p17, n74154_2_p4, n74154_2_p5, n74154_2_p6, n74154_2_p7, n74154_2_p8, n74154_2_p9, n74154_2_p10, n74154_2_p11, n74154_2_p12, n74154_2_p13, n74154_2_p14, n74154_2_p15, n74154_2_p16, n74154_2_p17, CONTROLWORD[11], CONTROLWORD[12], CONTROLWORD[13], CONTROLWORD[14], n74154_2_p22, n74154_2_p22, n74154_2_p6, n74154_2_p5, n74154_2_p4, n74154_2_p27, n74154_2_p28
  _74161_Bus u_74161_bus_6 (
    .CLK(and_20_out), .nCLR(nor_10_out), .nPE(1'b1), .CEP(1'b1), .CET(1'b1), .Q(n74161_bus_6_q));  // open: D, TC
  not not_15 (n74154_1_p15, FETCH_DONE);
  nand nand_15 (n74154_2_p22, not_16_out, FETCH_DONE);
  not not_16 (not_16_out, CONTROLWORD[15]);
  not not_17 (not_17_out, ic_74138_2_p7);
  // IC_74138 ic_74138_2: pin names not known; wires that end beside it: n74161_bus_6_q[0], n74161_bus_6_q[1], n74161_bus_6_q[2], 1'b0, 1'b0, nRESET, ic_74138_2_p7, ic_74138_2_p8, ic_74138_2_p9, not_17_out, ic_74138_2_p11, ic_74138_2_p12
  not not_18 (ic_74138_2_p11, ic_74138_2_p8);
  not not_19 (ic_74138_2_p12, ic_74138_2_p9);
  not not_20 (A_load, n74154_4_p1);
  not not_21 (B_load, n74154_4_p2);
  not not_22 (C_load, n74154_4_p3);
  not not_23 (H_load, n74154_4_p4);
  not not_24 (L_load, n74154_4_p5);
  not not_25 (ALU_load, n74154_4_p6);
  not not_26 (F_load, n74154_4_p7);
  not not_27 (PC_H_load, n74154_4_p11);
  not not_28 (PC_L_load, n74154_4_p20);
  not not_29 (STK_H_load, n74154_4_p19);
  not not_30 (STK_L_load, n74154_4_p18);
  not not_31 (MEM_out, n74154_3_p7);
  // _74154 74154_3: pin names not known; wires that end beside it: nA_out, nB_out, nC_out, nH_out, nL_out, nF_out, n74154_3_p7, nPC_H_out, CONTROLWORD[11], CONTROLWORD[12], CONTROLWORD[13], CONTROLWORD[14], n74154_3_p13, n74154_3_p13, nSTK_L_out, nSTK_H_out, nPC_L_out
  // _74154 74154_4: pin names not known; wires that end beside it: n74154_4_p1, n74154_4_p2, n74154_4_p3, n74154_4_p4, n74154_4_p5, n74154_4_p6, n74154_4_p7, nMAR_H_load, nMAR_L_load, nMEM_load, n74154_4_p11, CONTROLWORD[7], CONTROLWORD[8], CONTROLWORD[9], CONTROLWORD[10], n74154_4_p16, n74154_4_p16, n74154_4_p18, n74154_4_p19, n74154_4_p20
  nand nand_16 (n74154_4_p16, CONTROLWORD[15], FETCH_DONE);
  nand nand_17 (n74154_3_p13, CONTROLWORD[15], FETCH_DONE);

  assign out_7 = CONTROLWORD[5:1];
  assign {out_13[3], out_13[0]} = {Negative, Carry};
  assign Overflow = out_13[1];
  assign Zero = out_13[2];

  // Other names for the same wires on the sheet: Fc = Carry; FLAGS[3:0] = {Negative, out_13[2:1], Carry};
  //   Fo = out_13[1]; Fz = out_13[2]; Fn = Negative; TSTATE[3:0] = out_12; INSTRUCTION[7:0] = out_14;
  //   CW_ALU = CONTROLWORD[6]; CW_OPERATION = CONTROLWORD[15]; CW_ALU_OP[4:0] = CONTROLWORD[5:1];
  //   CW_FUNC1[3:0] = CONTROLWORD[4:1]; CW_OP_LOAD[3:0] = CONTROLWORD[10:7]; CW_FUNC0[3:0] = CONTROLWORD[14:11];
  //   CW_OP_OUT[3:0] = CONTROLWORD[14:11]; DATA[7:0] = in_1; PC_inc = IR_load

  // Notes on the sheet:
  //   NOT/AND only for Logisim
  //   STACK POINTER
  //   FLAGS REGISTER
  //   STK_H
  //   FETCH CYCLE
  //   ALU
  //   STK_L
  //   TSTATE COUNTER
  //   REGISTERS
  //   PC_H
  //   PC_H
  //   PC_L
  //   MEMORY ACCESS REGISTER
  //   contents of rom_1 (hex, n*v repeats v):
  //   16*800 240*0 16*8800 16*800 224*0 16*9000 16*800 224*0 16*9800 16*800 224*0 16*a000 16*800 224*0
  //   16*8080 16*800 224*0 16*9080 16*800 224*0 16*9880 16*800 224*0 16*a080 16*800 224*0 16*8100 16*800
  //   224*0 16*8900 16*800 224*0 16*9900 16*800 224*0 16*a100 16*800 224*0 16*8180 16*800 224*0 16*8980
  //   16*800 224*0 16*9180 16*800 224*0 16*a180 16*800 224*0 16*8200 16*800 224*0 16*8a00 16*800 224*0
  //   16*9200 16*800 224*0 16*9a00 16*800 224*0 16*9880 16*a100 16*800 208*0 16*8980 16*9200 16*800 208*0
  //   16*c80c 16*2802 224*0 16*c88c 16*2802 224*0 16*c90c 16*2802 224*0 16*c98c 16*2802 224*0 16*ca0c
  //   16*2802 12512*0 16*82d2 16*800 224*0 16*8ad2 16*800 224*0 16*92d2 16*800 224*0 16*9ad2 16*800 224*0
  //   16*a2d2 16*800 31456*0 16*300a 16*0 16*3000 32*0 16*2800 16*800 145*0 300a 0 300a 0 300a 0 300a 0
  //   300a 0 300a 0 300a 0 300a 17*0 3000 0 3000 0 3000 0 3000 0 3000 0 3000 0 3000 0 3000 33*0 2800 0
  //   2800 0 2800 0 2800 0 2800 0 2800 0 2800 0 2800 0 800 0 800 0 800 0 800 0 800 0 800 0 800 0 800
  //   PROGRAM COUNTER
  //   PC_L
  //   MAR_H
  //   MICROCODE ROM
  //   MAR_L
  //   TODO: Forgot MAR_inc
  //   CW_OPERATION=0 (function)
  //   CW_OPERATION=1 (data)
  //   MEMORY
  //   contents of rom_2 (hex, n*v repeats v):
  //   17 aa 18 bb d 12 0 0 17 cc
  //   used NAND to bring down no. of chips
  //   Replace OR gates with diode logic?
  //   BROKEN ASYNC RESET
  //   CONTROL WORD DECODING
endmodule

// CLOCK
module Clock_Phases (
  input  CLOCK,
  input  HALT,
  input  CONTINUE,
  output HALTED,
  output CLOCK1,
  output CLOCK2,
  output nCLOCK1,
  output nCLOCK2
);

  wire and_1_out, d_ff_2_q, d_ff_2_qn, d_ff_3_q, d_ff_3_qn, d_ff_4_q, not_1_out, not_2_out;

  D_Flip_Flop d_ff_1 (.clk(and_1_out), .D(HALT), .Q(HALTED), .reset(CONTINUE));  // open: Qn, preset, en
  not not_1 (not_1_out, HALTED);
  and and_1 (and_1_out, CLOCK, not_1_out);
  D_Flip_Flop d_ff_2 (.clk(and_1_out), .D(1'b1), .Q(d_ff_2_q), .Qn(d_ff_2_qn), .reset(d_ff_4_q));  // open: preset, en
  not not_2 (not_2_out, d_ff_3_q);
  D_Flip_Flop d_ff_3 (.clk(and_1_out), .D(d_ff_2_q), .Q(d_ff_3_q), .Qn(d_ff_3_qn));  // open: preset, en, reset
  and and_2 (CLOCK1, not_2_out, d_ff_2_q);
  and and_3 (CLOCK2, d_ff_3_q, d_ff_2_q);
  and and_4 (nCLOCK1, d_ff_3_q, d_ff_2_qn);
  and and_5 (nCLOCK2, d_ff_3_qn, d_ff_4_q, d_ff_2_qn);
  D_Flip_Flop d_ff_4 (.clk(and_1_out), .D(d_ff_3_q), .Q(d_ff_4_q));  // open: Qn, preset, en, reset
endmodule

module LCD_Decoder (
  input  [7:0] DATA,
  input  CLOCK,
  input  nLOAD,
  output RESET,
  output [15:0] COLOR,
  output LCD_CLOCK,
  output [6:0] X_COORD,
  output [6:0] Y_COORD
);

  wire and_1_out, and_3_out, dip_7474_1_p4, n74191_1_p13, n74191_1_p14, n74191_1_p15, n74191_1_p16,
       n74191_2_p13, n74191_3_p13, n74191_3_p14, nand_1_out, not_1_out, not_3_out, not_4_out, RESET_t;
  wire [7:5] ic_74377_1_p16;

  Pull_Resistor pull_resistor_1 (.node(DATA[0]));
  not not_1 (not_1_out, CLOCK);
  // IC_74377 ic_74377_1: pin names not known; wires that end beside it: DATA[0], DATA[1], DATA[2], DATA[3], DATA[4], DATA[5], DATA[6], DATA[7], not_1_out, nLOAD, COLOR[5], COLOR[6], COLOR[7], COLOR[8], COLOR[9], ic_74377_1_p16[5], ic_74377_1_p16[6], ic_74377_1_p16[7]
  and and_1 (and_1_out, ic_74377_1_p16[7], ic_74377_1_p16[6], ic_74377_1_p16[5], COLOR[9], COLOR[8], COLOR[7], COLOR[6], COLOR[5]);
  not not_2 (RESET_t, RESET);
  and and_2 (RESET, and_1_out, not_3_out);
  not not_3 (not_3_out, nLOAD);
  nand nand_1 (nand_1_out, CLOCK, nLOAD);
  and and_3 (and_3_out, CLOCK, not_3_out);
  and and_4 (LCD_CLOCK, RESET_t, dip_7474_1_p4);
  not not_4 (not_4_out, dip_7474_1_p4);
  // DIP_7474 dip_7474_1: pin names not known; wires that end beside it: nand_1_out, and_3_out, and_3_out, dip_7474_1_p4
  // _74191 74191_1: pin names not known; wires that end beside it: 1'b0, not_4_out, 1'b0, RESET_t, X_COORD[0], 1'b0, X_COORD[1], 1'b0, X_COORD[2], 1'b0, X_COORD[3], 1'b0, n74191_1_p13, n74191_1_p14, n74191_1_p15, n74191_1_p16
  // _74191 74191_2: pin names not known; wires that end beside it: 1'b0, n74191_1_p13, 1'b0, RESET_t, X_COORD[4], 1'b0, Y_COORD[0], 1'b0, Y_COORD[1], 1'b0, Y_COORD[2], 1'b0, n74191_2_p13
  // _74191 74191_3: pin names not known; wires that end beside it: 1'b0, n74191_2_p13, 1'b0, RESET_t, Y_COORD[3], 1'b0, Y_COORD[4], 1'b0, n74191_1_p14, 1'b0, n74191_1_p15, 1'b0, n74191_3_p13, n74191_3_p14
  // _74191 74191_4: pin names not known; wires that end beside it: 1'b0, n74191_3_p13, 1'b0, RESET_t, n74191_1_p16, 1'b0, n74191_3_p14, 1'b0, 1'b0, 1'b0

  assign {COLOR[15:10], COLOR[4:0]} = {11{1'b0}};
  assign X_COORD[6:5] = 2'b00;
  assign Y_COORD[6:5] = 2'b00;
endmodule

// 74161
module _74161_Clockfix (
  input  CLK,
  input  nCLR,
  input  nPE,
  input  CEP,
  input  CET,
  input  D1,
  input  D2,
  input  D3,
  input  D4,
  output Q1,
  output Q2,
  output Q3,
  output Q4,
  output TC
);

  wire and_1_out, and_2_out, and_3_out, and_4_out, and_5_out, and_6_out, and_7_out, and_8_out, and_9_out,
       and_10_out, and_11_out, and_12_out, not_1_out, not_2_out, or_1_out, or_2_out, or_3_out, or_4_out,
       xor_1_out, xor_2_out, xor_3_out, xor_4_out;

  not not_1 (not_1_out, nCLR);
  and and_1 (and_1_out, nPE, CEP, CET);
  not not_2 (not_2_out, nPE);
  and and_2 (and_2_out, D1, not_2_out);
  and and_3 (and_3_out, Q1, nPE);
  and and_4 (and_4_out, D2, not_2_out);
  and and_5 (and_5_out, Q2, nPE);
  and and_6 (and_6_out, Q1, and_1_out);
  and and_7 (and_7_out, D3, not_2_out);
  and and_8 (and_8_out, Q3, nPE);
  and and_9 (and_9_out, Q2, Q1, and_1_out);
  and and_10 (and_10_out, D4, not_2_out);
  and and_11 (and_11_out, Q4, nPE);
  and and_12 (and_12_out, Q3, Q2, Q1, and_1_out);
  xor xor_1 (xor_1_out, and_3_out, and_1_out);
  xor xor_2 (xor_2_out, and_5_out, and_6_out);
  xor xor_3 (xor_3_out, and_8_out, and_9_out);
  xor xor_4 (xor_4_out, and_11_out, and_12_out);
  or or_1 (or_1_out, and_2_out, xor_1_out);
  or or_2 (or_2_out, and_4_out, xor_2_out);
  or or_3 (or_3_out, and_7_out, xor_3_out);
  or or_4 (or_4_out, and_10_out, xor_4_out);
  // D_Flip_Flop d_flip_flop_1: pin names not known; wires that end beside it: or_1_out, CLK, not_1_out, Q1
  // D_Flip_Flop d_flip_flop_2: pin names not known; wires that end beside it: or_2_out, CLK, not_1_out, Q2
  // D_Flip_Flop d_flip_flop_3: pin names not known; wires that end beside it: or_3_out, CLK, not_1_out, Q3
  // D_Flip_Flop d_flip_flop_4: pin names not known; wires that end beside it: or_4_out, CLK, not_1_out, Q4
  and and_13 (TC, Q4, Q3, Q2, Q1, CET);
endmodule

module _74163_Clockfix (
  input  CLK,
  input  CE,
  input  LE,
  input  CEP,
  input  CET,
  input  D1,
  input  D2,
  input  D3,
  input  D4,
  output Q1,
  output Q2,
  output Q3,
  output Q4,
  output TC
);

  wire and_1_out, and_2_out, and_3_out, and_4_out, and_5_out, and_6_out, and_7_out, and_8_out, and_9_out,
       and_10_out, and_11_out, and_12_out, and_13_out, not_1_out, not_2_out, or_1_out, or_2_out, or_3_out,
       or_4_out, xor_1_out, xor_2_out, xor_3_out, xor_4_out;

  not not_1 (not_1_out, CE);
  and and_1 (and_1_out, LE, CEP, CET);
  not not_2 (not_2_out, LE);
  and and_2 (and_2_out, D1, not_1_out, not_2_out);
  and and_3 (and_3_out, Q1, not_1_out, LE);
  and and_4 (and_4_out, not_1_out, and_1_out);
  and and_5 (and_5_out, D2, not_1_out, not_2_out);
  and and_6 (and_6_out, Q2, not_1_out, LE);
  and and_7 (and_7_out, Q1, not_1_out, and_1_out);
  and and_8 (and_8_out, D3, not_1_out, not_2_out);
  and and_9 (and_9_out, Q3, not_1_out, LE);
  and and_10 (and_10_out, Q2, Q1, and_1_out, not_1_out);
  and and_11 (and_11_out, D4, not_1_out, not_2_out);
  and and_12 (and_12_out, Q4, not_1_out, LE);
  and and_13 (and_13_out, Q3, Q2, not_1_out, Q1, and_1_out);
  xor xor_1 (xor_1_out, and_3_out, and_4_out);
  xor xor_2 (xor_2_out, and_6_out, and_7_out);
  xor xor_3 (xor_3_out, and_9_out, and_10_out);
  xor xor_4 (xor_4_out, and_12_out, and_13_out);
  or or_1 (or_1_out, and_2_out, xor_1_out);
  or or_2 (or_2_out, and_5_out, xor_2_out);
  or or_3 (or_3_out, and_8_out, xor_3_out);
  or or_4 (or_4_out, and_11_out, xor_4_out);
  // D_Flip_Flop d_flip_flop_1: pin names not known; wires that end beside it: or_1_out, CLK, Q1
  // D_Flip_Flop d_flip_flop_2: pin names not known; wires that end beside it: or_2_out, CLK, Q2
  // D_Flip_Flop d_flip_flop_3: pin names not known; wires that end beside it: or_3_out, CLK, Q3
  // D_Flip_Flop d_flip_flop_4: pin names not known; wires that end beside it: or_4_out, CLK, Q4
  and and_14 (TC, Q4, Q3, Q2, Q1, CET);
endmodule

module _74574_Peek (
  input  nOE,
  input  CLK,
  input  [7:0] D,
  output [7:0] P,
  output [7:0] Q
);

  wire not_1_out;

  not not_1 (not_1_out, nOE);
  // D_Flip_Flop d_flip_flop_1: pin names not known; wires that end beside it: D[0], P[0]
  // D_Flip_Flop d_flip_flop_2: pin names not known; wires that end beside it: CLK, D[1], CLK, P[1]
  // D_Flip_Flop d_flip_flop_3: pin names not known; wires that end beside it: D[2], P[2]
  // D_Flip_Flop d_flip_flop_4: pin names not known; wires that end beside it: CLK, D[3], CLK, P[3]
  // D_Flip_Flop d_flip_flop_5: pin names not known; wires that end beside it: D[4], CLK, P[4]
  // D_Flip_Flop d_flip_flop_6: pin names not known; wires that end beside it: D[5], CLK, P[5]
  // D_Flip_Flop d_flip_flop_7: pin names not known; wires that end beside it: D[6], P[6]
  // D_Flip_Flop d_flip_flop_8: pin names not known; wires that end beside it: CLK, D[7], CLK, P[7]
  assign Q[0] = not_1_out ? P[0] : 1'bz;  // Controlled_Buffer controlled_buffer_1
  assign Q[1] = not_1_out ? P[1] : 1'bz;  // Controlled_Buffer controlled_buffer_2
  assign Q[2] = not_1_out ? P[2] : 1'bz;  // Controlled_Buffer controlled_buffer_3
  assign Q[3] = not_1_out ? P[3] : 1'bz;  // Controlled_Buffer controlled_buffer_4
  assign Q[4] = not_1_out ? P[4] : 1'bz;  // Controlled_Buffer controlled_buffer_5
  assign Q[5] = not_1_out ? P[5] : 1'bz;  // Controlled_Buffer controlled_buffer_6
  assign Q[6] = not_1_out ? P[6] : 1'bz;  // Controlled_Buffer controlled_buffer_7
  assign Q[7] = not_1_out ? P[7] : 1'bz;  // Controlled_Buffer controlled_buffer_8

  // Notes on the sheet:
  //   This is the 74x574 chip, but with a PEEK output that always outputs the value stored in ther register
endmodule

module _74161_Bus (
  input  CLK,
  input  nCLR,
  input  nPE,
  input  CEP,
  input  CET,
  input  [3:0] D,
  output [3:0] Q,
  output TC
);

  wire and_1_out, and_2_out, and_3_out, and_4_out, and_5_out, and_6_out, and_7_out, and_8_out, and_9_out,
       and_10_out, and_11_out, and_12_out, not_1_out, not_2_out, or_1_out, or_2_out, or_3_out, or_4_out,
       xor_1_out, xor_2_out, xor_3_out, xor_4_out;

  not not_1 (not_1_out, nCLR);
  and and_1 (and_1_out, nPE, CEP, CET);
  not not_2 (not_2_out, nPE);
  and and_2 (and_2_out, D[0], not_2_out);
  and and_3 (and_3_out, Q[0], nPE);
  and and_4 (and_4_out, D[1], not_2_out);
  and and_5 (and_5_out, Q[1], nPE);
  and and_6 (and_6_out, Q[0], and_1_out);
  and and_7 (and_7_out, D[2], not_2_out);
  and and_8 (and_8_out, Q[2], nPE);
  and and_9 (and_9_out, Q[1], Q[0], and_1_out);
  and and_10 (and_10_out, D[3], not_2_out);
  and and_11 (and_11_out, Q[3], nPE);
  and and_12 (and_12_out, Q[2], Q[1], Q[0], and_1_out);
  xor xor_1 (xor_1_out, and_3_out, and_1_out);
  xor xor_2 (xor_2_out, and_5_out, and_6_out);
  xor xor_3 (xor_3_out, and_8_out, and_9_out);
  xor xor_4 (xor_4_out, and_11_out, and_12_out);
  or or_1 (or_1_out, and_2_out, xor_1_out);
  or or_2 (or_2_out, and_4_out, xor_2_out);
  or or_3 (or_3_out, and_7_out, xor_3_out);
  or or_4 (or_4_out, and_10_out, xor_4_out);
  // D_Flip_Flop d_flip_flop_1: pin names not known; wires that end beside it: or_1_out, CLK, not_1_out, Q[0]
  // D_Flip_Flop d_flip_flop_2: pin names not known; wires that end beside it: or_2_out, CLK, not_1_out, Q[1]
  // D_Flip_Flop d_flip_flop_3: pin names not known; wires that end beside it: or_3_out, CLK, not_1_out, Q[2]
  // D_Flip_Flop d_flip_flop_4: pin names not known; wires that end beside it: or_4_out, CLK, not_1_out, Q[3]
  and and_13 (TC, Q[3], Q[2], Q[1], Q[0], CET);
endmodule

// 74245
module _74245_Bus (
  input  [7:0] A,
  input  nOE,
  output [7:0] B
);

  wire not_1_out, not_2_out;

  not not_1 (not_1_out, nOE);
  not not_2 (not_2_out, nOE);
  assign B[0] = not_1_out ? A[0] : 1'bz;  // Controlled_Buffer controlled_buffer_1
  assign B[1] = not_1_out ? A[1] : 1'bz;  // Controlled_Buffer controlled_buffer_2
  assign B[2] = not_1_out ? A[2] : 1'bz;  // Controlled_Buffer controlled_buffer_3
  assign B[3] = not_1_out ? A[3] : 1'bz;  // Controlled_Buffer controlled_buffer_4
  assign B[4] = not_2_out ? A[4] : 1'bz;  // Controlled_Buffer controlled_buffer_5
  assign B[5] = not_2_out ? A[5] : 1'bz;  // Controlled_Buffer controlled_buffer_6
  assign B[6] = not_2_out ? A[6] : 1'bz;  // Controlled_Buffer controlled_buffer_7
  assign B[7] = not_2_out ? A[7] : 1'bz;  // Controlled_Buffer controlled_buffer_8
endmodule

// 74191
module _74191_Bus (
  input  nU_D,
  input  CK,
  input  nCTEN,
  input  nPL,
  input  [3:0] D,
  output [3:0] Q,
  output TC,
  output nRCO
);

  wire and_1_out, and_2_out, and_3_out, and_4_out, and_5_out, and_6_out, and_7_out, and_8_out,
       jk_flipflop_1_p4, jk_flipflop_1_p5, jk_flipflop_1_p7, jk_flipflop_2_p4, jk_flipflop_2_p5,
       jk_flipflop_2_p7, jk_flipflop_3_p4, jk_flipflop_3_p7, jk_flipflop_4_p4, jk_flipflop_4_p5, nand_5_out,
       nor_1_out, not_1_out, not_2_out, not_3_out, not_4_out, not_5_out, not_6_out, not_7_out, not_8_out,
       not_9_out, or_1_out, or_2_out, or_3_out;

  not not_1 (not_1_out, nCTEN);
  not not_2 (not_2_out, nU_D);
  // JK_FlipFlop jk_flipflop_1: pin names not known; wires that end beside it: not_1_out, CK, not_1_out, jk_flipflop_1_p4, jk_flipflop_1_p5, Q[0], jk_flipflop_1_p7
  nand nand_1 (jk_flipflop_1_p5, not_3_out, not_4_out);
  not not_3 (not_3_out, nPL);
  not not_4 (not_4_out, D[0]);
  not not_5 (not_5_out, nU_D);
  nand nand_2 (jk_flipflop_1_p4, not_3_out, D[0]);
  and and_1 (and_1_out, Q[0], not_5_out, not_1_out);
  or or_1 (or_1_out, and_1_out, and_2_out);
  and and_2 (and_2_out, nU_D, jk_flipflop_1_p7, not_1_out);
  // JK_FlipFlop jk_flipflop_2: pin names not known; wires that end beside it: or_1_out, CK, or_1_out, jk_flipflop_2_p4, jk_flipflop_2_p5, Q[1], jk_flipflop_2_p7
  nand nand_3 (jk_flipflop_2_p5, not_3_out, not_6_out);
  nand nand_4 (jk_flipflop_2_p4, not_3_out, D[1]);
  not not_6 (not_6_out, D[1]);
  and and_3 (and_3_out, and_1_out, Q[1], not_1_out);
  and and_4 (and_4_out, and_2_out, jk_flipflop_2_p7, not_1_out);
  or or_2 (or_2_out, and_3_out, and_4_out);
  nand nand_5 (nand_5_out, not_3_out, not_7_out);
  // JK_FlipFlop jk_flipflop_3: pin names not known; wires that end beside it: or_2_out, CK, or_2_out, jk_flipflop_3_p4, nand_5_out, Q[2], jk_flipflop_3_p7
  nand nand_6 (jk_flipflop_3_p4, not_3_out, D[2]);
  not not_7 (not_7_out, D[2]);
  and and_5 (and_5_out, and_3_out, Q[2], not_1_out);
  and and_6 (and_6_out, and_4_out, jk_flipflop_3_p7, not_1_out);
  or or_3 (or_3_out, and_5_out, and_6_out);
  // JK_FlipFlop jk_flipflop_4: pin names not known; wires that end beside it: or_3_out, CK, or_3_out, jk_flipflop_4_p4, jk_flipflop_4_p5, Q[3]
  nand nand_7 (jk_flipflop_4_p5, not_3_out, not_8_out);
  not not_8 (not_8_out, D[3]);
  not not_9 (not_9_out, CK);
  nand nand_8 (jk_flipflop_4_p4, not_3_out, D[3]);
  Hex_Digit_Display hex_digit_display_1 (.value(Q));  // open: dp
  nor nor_1 (nor_1_out, Q[3], Q[2], Q[1], Q[0], not_2_out);
  and and_7 (and_7_out, not_2_out, Q[3], Q[2], Q[1], Q[0]);
  or or_4 (TC, nor_1_out, and_7_out);
  and and_8 (and_8_out, TC, not_1_out, not_9_out);
  not not_10 (nRCO, and_8_out);
endmodule

// 74377
module _74377_Bus (
  input  [7:0] D,
  input  CLK,
  input  nCE,
  output [7:0] Q
);

  wire and_1_out, not_1_out;

  not not_1 (not_1_out, nCE);
  and and_1 (and_1_out, CLK, not_1_out);
  // D_Flip_Flop d_flip_flop_1: pin names not known; wires that end beside it: D[0], and_1_out, Q[0]
  // D_Flip_Flop d_flip_flop_2: pin names not known; wires that end beside it: D[1], and_1_out, Q[1]
  // D_Flip_Flop d_flip_flop_3: pin names not known; wires that end beside it: D[2], and_1_out, Q[2]
  // D_Flip_Flop d_flip_flop_4: pin names not known; wires that end beside it: D[3], and_1_out, Q[3]
  // D_Flip_Flop d_flip_flop_5: pin names not known; wires that end beside it: D[4], and_1_out, Q[4]
  // D_Flip_Flop d_flip_flop_6: pin names not known; wires that end beside it: D[5], and_1_out, Q[5]
  // D_Flip_Flop d_flip_flop_7: pin names not known; wires that end beside it: D[6], and_1_out, Q[6]
  // D_Flip_Flop d_flip_flop_8: pin names not known; wires that end beside it: D[7], and_1_out, Q[7]
endmodule

module tmp (
  input  in_1,
  input  in_2,
  input  in_3,
  input  in_4,
  input  in_5,
  output [3:0] out_6
);

  wire and_1_out, and_2_out, and_3_out, and_4_out, and_5_out, and_6_out, and_8_out, button_1_out, CLOCK1,
       CLOCK2, clock_1_out, clock_phases_1_halted, CONTINUE_out, FETCH_0, FETCH_1, FETCH_DONE, ic_74138_1_p7,
       ic_74138_1_p8, ic_74138_1_p9, ic_74138_1_p10, IR_load, n74163_clockfix_1_q1, n74163_clockfix_1_q2,
       n74163_clockfix_1_q3, nCLOCK1, nCLOCK2, nMEM_out, not_1_out, not_2_out, nPC_MAR_transfer, nRESET,
       or_1_out, or_2_out, or_3_out, TSTATE_MAX, TSTATE_reset;

  LED led_1 (.in(clock_phases_1_halted));
  Button button_1 (.out(button_1_out));
  Button CONTINUE (.out(CONTINUE_out));
  not not_1 (not_1_out, FETCH_DONE);
  not not_2 (not_2_out, nRESET);
  Clock clock_1 (.out(clock_1_out));
  and and_1 (and_1_out, nCLOCK1, FETCH_0);
  and and_2 (and_2_out, nCLOCK2, FETCH_1);
  or or_1 (or_1_out, not_2_out, TSTATE_reset, TSTATE_MAX);
  Clock_Phases clock_phases_1 (
    .CLOCK(clock_1_out), .HALT(button_1_out), .CONTINUE(CONTINUE_out), .HALTED(clock_phases_1_halted),
    .CLOCK1(CLOCK1), .CLOCK2(CLOCK2), .nCLOCK1(nCLOCK1), .nCLOCK2(nCLOCK2));
  or or_2 (or_2_out, CLOCK1, and_1_out, and_2_out);
  and and_3 (and_3_out, or_2_out, or_3_out);
  or or_3 (or_3_out, not_1_out, or_1_out);
  and and_4 (and_4_out, FETCH_0, CLOCK2);
  and and_5 (and_5_out, in_5, nCLOCK1);
  _74163_Clockfix u_74163_clockfix_1 (
    .CLK(and_3_out), .CE(or_1_out), .LE(1'b1), .CEP(1'b1), .CET(1'b1), .D1(1'b0), .D2(1'b0), .D3(1'b0),
    .D4(1'b0), .Q1(n74163_clockfix_1_q1), .Q2(n74163_clockfix_1_q2), .Q3(n74163_clockfix_1_q3));  // open: Q4, TC
  nor nor_1 (nPC_MAR_transfer, and_4_out, in_3);
  nor nor_2 (nMEM_out, FETCH_1, in_4);
  and and_6 (and_6_out, FETCH_DONE, nCLOCK2);
  or or_4 (IR_load, and_6_out, and_5_out);
  not not_3 (nRESET, in_1);
  // IC_74138 ic_74138_1: pin names not known; wires that end beside it: n74163_clockfix_1_q1, n74163_clockfix_1_q2, n74163_clockfix_1_q3, 1'b0, 1'b0, nRESET, ic_74138_1_p7, ic_74138_1_p8, ic_74138_1_p9, ic_74138_1_p10
  not not_4 (FETCH_0, ic_74138_1_p7);
  not not_5 (FETCH_1, ic_74138_1_p8);
  not not_6 (FETCH_DONE, ic_74138_1_p9);
  and and_7 (TSTATE_reset, in_2, nCLOCK2);
  not not_7 (ic_74138_1_p10, TSTATE_reset);
  and and_8 (and_8_out, ic_74138_1_p10, FETCH_DONE);
  _74161_Clockfix u_74161_clockfix_1 ();  // open: CLK, nCLR, nPE, CEP, CET, D1, D4, Q1, Q2, Q3, Q4, TC, D3, D2
  Pull_Resistor pull_resistor_1 (.node(TSTATE_MAX));
  _74161_Bus u_74161_bus_1 (
    .CLK(CLOCK1), .nCLR(and_8_out), .nPE(1'b1), .CEP(1'b1), .CET(1'b1), .Q(out_6), .TC(TSTATE_MAX));  // open: D

  // Other names for the same wires on the sheet: MEM_out = in_4; PC_inc = IR_load; PC_inc_rom = in_5;
  //   PC_MAR_transfer = in_3; TSTATE[3:0] = out_6

  // Notes on the sheet:
  //   FETCH CYCLE
  //   TSTATE COUNTER
endmodule

module tmp2 (
  input  in_1,
  input  in_2,
  input  in_3,
  input  in_4,
  input  in_5,
  output [3:0] out_6
);

  wire and_1_out, and_2_out, and_3_out, and_4_out, and_5_out, and_6_out, and_7_out, and_9_out, button_1_out,
       CLOCK1, CLOCK2, clock_1_out, clock_phases_1_halted, CONTINUE_out, FETCH_0, FETCH_1, FETCH_DONE,
       ic_74138_1_p7, ic_74138_1_p8, ic_74138_1_p9, IR_load, n74161_clockfix_1_q2, n74161_clockfix_1_q3,
       n74161_clockfix_1_q4, nCLOCK1, nCLOCK2, nMEM_out, nor_1_out, not_1_out, not_2_out, not_7_out,
       nPC_MAR_transfer, nRESET, or_1_out, TSTATE_MAX, TSTATE_reset;

  LED led_1 (.in(clock_phases_1_halted));
  Button button_1 (.out(button_1_out));
  Button CONTINUE (.out(CONTINUE_out));
  not not_1 (not_1_out, nRESET);
  Clock clock_1 (.out(clock_1_out));
  nor nor_1 (nor_1_out, not_1_out, TSTATE_reset, TSTATE_MAX);
  not not_2 (not_2_out, FETCH_DONE);
  and and_1 (and_1_out, nCLOCK1, FETCH_0);
  and and_2 (and_2_out, nCLOCK2, FETCH_1);
  Clock_Phases clock_phases_1 (
    .CLOCK(clock_1_out), .HALT(button_1_out), .CONTINUE(CONTINUE_out), .HALTED(clock_phases_1_halted),
    .CLOCK1(CLOCK1), .CLOCK2(CLOCK2), .nCLOCK1(nCLOCK1), .nCLOCK2(nCLOCK2));
  and and_3 (and_3_out, nor_1_out, not_2_out);
  and and_4 (and_4_out, and_3_out, or_1_out);
  or or_1 (or_1_out, CLOCK1, and_1_out, and_2_out);
  and and_5 (and_5_out, FETCH_0, CLOCK2);
  and and_6 (and_6_out, in_5, nCLOCK1);
  _74161_Clockfix u_74161_clockfix_1 (
    .CLK(and_4_out), .nCLR(nor_1_out), .nPE(1'b1), .CEP(1'b1), .CET(1'b1), .Q2(n74161_clockfix_1_q2),
    .Q3(n74161_clockfix_1_q3), .Q4(n74161_clockfix_1_q4));  // open: D1, D4, Q1, TC, D3, D2
  nor nor_2 (nPC_MAR_transfer, and_5_out, in_3);
  nor nor_3 (nMEM_out, FETCH_1, in_4);
  and and_7 (and_7_out, FETCH_DONE, nCLOCK2);
  or or_2 (IR_load, and_7_out, and_6_out);
  // IC_74138 ic_74138_1: pin names not known; wires that end beside it: n74161_clockfix_1_q2, n74161_clockfix_1_q3, n74161_clockfix_1_q4, 1'b0, 1'b0, nRESET, ic_74138_1_p7, ic_74138_1_p8, ic_74138_1_p9
  not not_3 (nRESET, in_1);
  not not_4 (FETCH_0, ic_74138_1_p7);
  not not_5 (FETCH_1, ic_74138_1_p8);
  not not_6 (FETCH_DONE, ic_74138_1_p9);
  and and_8 (TSTATE_reset, in_2, nCLOCK2);
  not not_7 (not_7_out, TSTATE_reset);
  and and_9 (and_9_out, not_7_out, FETCH_DONE);
  Pull_Resistor pull_resistor_1 (.node(TSTATE_MAX));
  _74161_Bus u_74161_bus_1 (
    .CLK(CLOCK1), .nCLR(and_9_out), .nPE(1'b1), .CEP(1'b1), .CET(1'b1), .Q(out_6), .TC(TSTATE_MAX));  // open: D
  _74163_Clockfix u_74163_clockfix_1 ();  // open: CLK, CE, LE, CEP, CET, D1, D2, D3, D4, Q1, Q2, Q3, Q4, TC

  // Other names for the same wires on the sheet: MEM_out = in_4; PC_inc = IR_load; PC_inc_rom = in_5;
  //   PC_MAR_transfer = in_3; TSTATE[3:0] = out_6

  // Notes on the sheet:
  //   FETCH CYCLE
  //   TSTATE COUNTER
endmodule
